# Fritzing sketch Untitled Sketch (saved by Fritzing 0.9.3b)
circuit board: 8.46667cm x 5.64444cm
breadboards: 1

parts:
  Q1 = NPN-Transistor [package="TO92 [THT]"]
  R1 = Resistor [tolerance=±5% resistance=220 package=THT]
  D1 = Rectifier Diode [part_number=1N4001 package="300 mil [THT]"]
  Componente2 = Bluetooth Mate Silver
  J1 = screw terminal, 3 pins
  J7 = female pin header, 3 pins [form="♀ (female)"]
  J6 = female pin header, 8 pins [form="♀ (female)"]
  Componente1 = Arduino Uno (Rev3)
  J8 = screw terminal, 3 pins
  D2 = Rectifier Diode [part_number=1N4001 package="300 mil [THT]"]

nets:
  GND: Q1.E, Componente2.GND, J1.pin3, J7.pin1, J6.pin5, Componente1.GND, J8.pin2
  N1: Q1.B, R1.Pin_1
  N2: Q1.C, D1.anode, J1.pin1
  N3: R1.Pin_0, Componente1.D3_PWM
  N4: D1.cathode, J1.pin2, J8.pin3
  N5: Componente2.RX_5V, Componente1.D1/TX
  N6: Componente2.TX_5V, Componente1.D0/RX
  VCC: Componente2.VCC, J7.pin2, J6.pin6, Componente1.5V, D2.cathode
  N7: J7.pin3, Componente1.D2
  N8: J6.pin1, Componente1.D10_PWM/SS
  N9: J6.pin2, Componente1.D9_PWM
  N10: J6.pin3, Componente1.D8
  N11: J6.pin4, Componente1.D7
  N12: J6.pin7, Componente1.A4/SDA
  N13: J6.pin8, Componente1.A5/SCL
  N14: J8.pin1, D2.anode
